# Fritzing sketch 3LEDky (saved by Fritzing 0.9.3b)
circuit board: 8.46667cm x 5.64444cm
breadboards: 1

parts:
  WeMos_D1_Mini1 = WeMos D1 Mini
  R1 = Resistor [tolerance=±5% resistance=220 package=THT]
  R2 = Resistor [tolerance=±5% resistance=220 package=THT]
  R3 = Resistor [tolerance=±5% resistance=220 package=THT]
  LED2 = LED - 5mm [color="Blue (430nm)" package="5 mm [THT]"]
  LED4 = LED - 5mm [color="Green (555nm)" package="5 mm [THT]"]
  LED3 = LED - 5mm [color="Red (633nm)" package="5 mm [THT]"]

nets:
  N1: WeMos_D1_Mini1.D1, LED2.anode
  N2: WeMos_D1_Mini1.D2, LED3.anode
  N3: WeMos_D1_Mini1.D3, LED4.anode
  N4: WeMos_D1_Mini1.G, R1.Pin_1, R2.Pin_1, R3.Pin_1
  N5: R1.Pin_0, LED4.cathode
  N6: R2.Pin_0, LED3.cathode
  N7: R3.Pin_0, LED2.cathode
