# Fritzing sketch LEDka (saved by Fritzing 0.9.3b)
circuit board: 8.46667cm x 5.64444cm
breadboards: 1

parts:
  WeMos_D1_Mini1 = WeMos D1 Mini
  cervena = smd LED [color="Red (633nm)" package="0805 [SMD]"]
  rezistor = Resistor [tolerance=±5% resistance=220 package=THT]

nets:
  N1: WeMos_D1_Mini1.D1, cervena.anode
  N2: WeMos_D1_Mini1.G, rezistor.Pin_0
  N3: cervena.cathode, rezistor.Pin_1
