# Fritzing sketch RGB-LEDka (saved by Fritzing 0.9.3b)
breadboards: 1

parts:
  WeMos_D1_Mini1 = WeMos D1 Mini
  R2 = Resistor [tolerance=±5% resistance=220 package=THT]
  R3 = Resistor [tolerance=±5% resistance=220 package=THT]
  R1 = Resistor [tolerance=±5% resistance=220 package=THT]
  RGB_dioda = RGB LED (com. cathode, rgb) [package="5 mm [THT]"]

nets:
  N1: WeMos_D1_Mini1.D6, R1.Pin_1
  N2: WeMos_D1_Mini1.D7, R2.Pin_1
  N3: WeMos_D1_Mini1.D8, R3.Pin_1
  N4: WeMos_D1_Mini1.G, RGB_dioda.common_cathode
  N5: R2.Pin_0, RGB_dioda.green_anode
  N6: R3.Pin_0, RGB_dioda.red_anode
  N7: R1.Pin_0, RGB_dioda.blue_anode
