# Fritzing sketch tlacitko-led (saved by Fritzing 0.9.3b)
breadboards: 1

parts:
  R1 = Resistor [tolerance=±5% resistance=4.7k package=THT]
  R2 = Resistor [tolerance=±5% resistance=330 package=THT]
  Tlačítko = Momentary Switch [package=ksa_sealed_tac_switch]
  LED = LED - 5mm [color="Red (633nm)" package="5 mm [THT]"]
  R3 = Resistor [tolerance=±5% resistance=220 package=THT]
  WeMos_D1_Mini1 = WeMos D1 Mini

nets (from the schematic view):
  N1: R1.Pin_0, Tlačítko.3, WeMos_D1_Mini1.D1
  N2: R1.Pin_1, R3.Pin_0, WeMos_D1_Mini1.G
  N3: R2.Pin_0, Tlačítko.1
  N4: R2.Pin_1, WeMos_D1_Mini1.3V3
  N5: LED.cathode, R3.Pin_1
  N6: LED.anode, WeMos_D1_Mini1.D2
