# Fritzing sketch tlacitko (saved by Fritzing 0.9.3b)
breadboards: 1

parts:
  WeMos_D1_Mini1 = WeMos D1 Mini
  R1 = Resistor [tolerance=±5% resistance=4.7k package=THT]
  R2 = Resistor [tolerance=±5% resistance=330 package=THT]
  Tlačítko = Momentary Switch [package=ksa_sealed_tac_switch]

nets (from the schematic view):
  N1: WeMos_D1_Mini1.3V3, R2.Pin_1
  N2: WeMos_D1_Mini1.D1, R1.Pin_0, Tlačítko.3
  N3: WeMos_D1_Mini1.G, R1.Pin_1
  N4: R2.Pin_0, Tlačítko.1
