# Fritzing sketch zaklad1 (saved by Fritzing 0.9.3b)
breadboards: 1

parts:
  WeMos_D1_Mini2 = WeMos D1 Mini
  R1 = Resistor [tolerance=±5% resistance=220 package=THT]
  LED1 = smd LED [color="Red (633nm)" package="0603 [SMD]"]

nets:
  N1: WeMos_D1_Mini2.3V3, LED1.anode
  N2: WeMos_D1_Mini2.G, R1.Pin_1
  N3: R1.Pin_0, LED1.cathode
